// Logisim project 16bit_CPU.circ as structural Verilog
module project_alu (
  input  [15:0] A,
  input  [15:0] B,
  input  ALU_OE,
  input  [3:0] AUSel,
  input  [2:0] RUSel,
  output [15:0] AUResult,
  output [15:0] AUDout,
  output RUResult
);

  project_ao project_ao_1 (.A(A), .B(B), .ALU_OE(ALU_OE), .AUSel(AUSel), .AUResult(AUResult), .AUDout(AUDout));
  project_ro project_ro_1 (.A(A), .B(B), .RUSel(RUSel), .RUResult(RUResult));
endmodule

module project_ao (
  input  [15:0] A,
  input  [15:0] B,
  input  ALU_OE,
  input  [3:0] AUSel,
  output [15:0] AUResult,
  output [15:0] AUDout
);

  wire [15:0] adder_1_out, and_1_out, divider_1_out, divider_2_rem, multiplexer_1_out, multiplier_1_out,
       negator_1_out, negator_2_out, or_1_out, shifter_1_out, shifter_2_out, shifter_3_out, shifter_4_out,
       subtractor_1_out, xor_1_out;

  Adder #(.width(16)) adder_1 (.a(A), .b(B), .out(adder_1_out));  // open: cin, cout
  assign and_1_out = A & B;  // AND_Gate and_1, 16 bits wide
  assign or_1_out = A | B;  // OR_Gate or_1, 16 bits wide
  assign xor_1_out = A ^ B;  // XOR_Gate xor_1, 16 bits wide
  Divider #(.width(16)) divider_1 (.a(A), .b(B), .out(divider_1_out));  // open: upper, rem
  Divider #(.width(16)) divider_2 (.a(A), .b(B), .rem(divider_2_rem));  // open: out, upper
  Multiplier #(.width(16)) multiplier_1 (.a(A), .b(B), .out(multiplier_1_out));  // open: cin, cout
  Subtractor #(.width(16)) subtractor_1 (.a(A), .b(B), .out(subtractor_1_out));  // open: bin, bout
  Shifter #(.width(16)) shifter_1 (.in(A), .\dist (4'b0010), .out(shifter_1_out));
  Shifter #(.width(16)) shifter_2 (.in(B), .\dist (4'b0010), .out(shifter_2_out));
  Shifter #(.shift("lr"), .width(16)) shifter_3 (.in(A), .\dist (4'b0010), .out(shifter_3_out));
  Shifter #(.shift("lr"), .width(16)) shifter_4 (.in(B), .\dist (4'b0010), .out(shifter_4_out));
  Negator #(.width(16)) negator_1 (.in(A), .out(negator_1_out));
  Negator #(.width(16)) negator_2 (.in(B), .out(negator_2_out));
  Multiplexer #(.select(4), .width(16)) multiplexer_1 (
    .in0(adder_1_out), .in1(and_1_out), .in2(or_1_out), .in3(xor_1_out), .in4(divider_1_out),
    .in5(divider_2_rem), .in6(multiplier_1_out), .in7(subtractor_1_out), .in8(shifter_1_out),
    .in9(shifter_2_out), .in10(shifter_3_out), .in11(shifter_4_out), .in12(negator_1_out),
    .in13(negator_2_out), .out(multiplexer_1_out), .sel(AUSel));  // open: in14, in15
  assign AUDout = ALU_OE ? multiplexer_1_out : 16'bz;  // Controlled_Buffer controlled_buffer_1

  assign AUResult = AUDout;
endmodule

module project_ro (
  input  [15:0] A,
  input  [15:0] B,
  input  [2:0] RUSel,
  output RUResult
);

  wire comparator_1_eq, comparator_1_gt, comparator_1_lt, not_1_out, or_1_out, or_2_out;

  Comparator #(.width(16)) comparator_1 (
    .a(A), .b(B), .gt(comparator_1_gt), .eq(comparator_1_eq), .lt(comparator_1_lt));
  or or_1 (or_1_out, comparator_1_gt, comparator_1_eq);
  or or_2 (or_2_out, comparator_1_eq, comparator_1_lt);
  not not_1 (not_1_out, comparator_1_eq);
  Multiplexer #(.select(3)) multiplexer_1 (
    .in0(comparator_1_gt), .in1(comparator_1_eq), .in2(or_1_out), .in3(comparator_1_lt), .in4(or_2_out),
    .in5(not_1_out), .out(RUResult), .sel(RUSel));  // open: in6, in7
endmodule

module Datapath (
  input  WE_MAR,
  input  Reset_MAR,
  input  OE_MAR,
  input  [15:0] TestData,
  input  Test_OE,
  input  internal_OE_MBR,
  input  WE_IR,
  input  clk,
  input  Reset_IR,
  input  WE_MBR,
  input  OE_IR,
  input  Reset_MBR,
  input  OE_MBR,
  input  WE_A,
  input  Reg_AB_Reset,
  input  Reg_AB_OE,
  input  WE_OR,
  input  Reset_OR,
  input  ALU_OE,
  input  [3:0] AUSel,
  input  OE_OR,
  input  [2:0] RUSel,
  input  WE_B,
  output [7:0] Result_MAR,
  output [15:0] IR_Result,
  output [15:0] Result_MBR,
  output [15:0] Result_A,
  output [15:0] Result_OR,
  output [15:0] AUResult,
  output RUResult,
  output [15:0] Result_B
);

  wire [7:0] bitselector_1_out, Instruction_Register_eight_lsbs, mar_1_dout;
  wire [15:0] ALU_audout;

  register_file Instruction_Register (
    .Data(ALU_audout), .WE(WE_IR), .clk(clk), .reset(Reset_IR), .OE(OE_IR), .Result(IR_Result),
    .Eight_LSBs(Instruction_Register_eight_lsbs));  // open: Dout, Eight_MSBs
  register_file A (
    .Data(ALU_audout), .WE(WE_A), .clk(clk), .reset(Reg_AB_Reset), .OE(Reg_AB_OE), .Result(Result_A));  // open: Dout, Eight_LSBs, Eight_MSBs
  project_alu ALU (
    .A(Result_A), .B(Result_B), .ALU_OE(ALU_OE), .AUSel(AUSel), .RUSel(RUSel), .AUResult(AUResult),
    .AUDout(ALU_audout), .RUResult(RUResult));
  register_file B (
    .Data(ALU_audout), .WE(WE_B), .clk(clk), .reset(Reg_AB_Reset), .OE(Reg_AB_OE), .Result(Result_B));  // open: Dout, Eight_LSBs, Eight_MSBs
  BitSelector #(.group(8)) bitselector_1 (.in(Instruction_Register_eight_lsbs), .out(bitselector_1_out), .sel(1'b0));
  LED led_1 (.in(ALU_audout[15]));
  LED led_2 (.in(ALU_audout[14]));
  assign ALU_audout = Test_OE ? TestData : 16'bz;  // Controlled_Buffer controlled_buffer_1
  LED led_3 (.in(ALU_audout[13]));
  LED led_4 (.in(ALU_audout[12]));
  LED led_5 (.in(ALU_audout[11]));
  LED led_6 (.in(ALU_audout[10]));
  LED led_7 (.in(ALU_audout[9]));
  LED led_8 (.in(ALU_audout[8]));
  LED led_9 (.in(ALU_audout[7]));
  LED led_10 (.in(ALU_audout[6]));
  LED led_11 (.in(ALU_audout[5]));
  LED led_12 (.in(ALU_audout[4]));
  LED led_13 (.in(ALU_audout[3]));
  LED led_14 (.in(ALU_audout[2]));
  LED led_15 (.in(ALU_audout[1]));
  LED led_16 (.in(ALU_audout[0]));
  assign ALU_audout = internal_OE_MBR ? Result_MBR : 16'bz;  // Controlled_Buffer controlled_buffer_2
  MAR mar_1 (
    .Data(bitselector_1_out), .WE(WE_MAR), .clk(clk), .reset(Reset_MAR), .OE(OE_MAR), .Result(Result_MAR),
    .Dout(mar_1_dout));
  register_file MBR (
    .Data(ALU_audout), .WE(WE_MBR), .clk(clk), .reset(Reset_MBR), .OE(OE_MBR), .Result(Result_MBR),
    .Dout(ALU_audout));  // open: Eight_LSBs, Eight_MSBs
  register_file Output_Register (
    .Data(ALU_audout), .WE(WE_OR), .clk(clk), .reset(Reset_OR), .OE(OE_OR), .Result(Result_OR),
    .Dout(ALU_audout));  // open: Eight_LSBs, Eight_MSBs
  LED led_17 (.in(ALU_audout[15]));
  LED led_18 (.in(ALU_audout[14]));
  LED led_19 (.in(ALU_audout[13]));
  LED led_20 (.in(ALU_audout[12]));
  LED led_21 (.in(ALU_audout[11]));
  LED led_22 (.in(ALU_audout[10]));
  LED led_23 (.in(ALU_audout[9]));
  LED led_24 (.in(ALU_audout[8]));
  LED led_25 (.in(ALU_audout[7]));
  LED led_26 (.in(ALU_audout[6]));
  LED led_27 (.in(ALU_audout[5]));
  LED led_28 (.in(ALU_audout[4]));
  LED led_29 (.in(ALU_audout[3]));
  LED led_30 (.in(ALU_audout[2]));
  LED led_31 (.in(ALU_audout[1]));
  LED led_32 (.in(ALU_audout[0]));

  // Notes on the sheet:
  //   D14
  //   D15
  //   D13
  //   D12
  //   D11
  //   D10
  //   D9
  //   Internal Data Bus
  //   D8
  //   D7
  //   D6
  //   D5
  //   D4
  //   D3
  //   D2
  //   D1
  //   D0
  //   External Data Bus
  //   D14
  //   D15
  //   D13
  //   D12
  //   D11
  //   D10
  //   D9
  //   D8
  //   D7
  //   D6
  //   D5
  //   D4
  //   D3
  //   D2
  //   D1
  //   D0
endmodule

module register_file (
  input  [15:0] Data,
  input  WE,
  input  clk,
  input  reset,
  input  OE,
  output [15:0] Result,
  output [15:0] Dout,
  output [7:0] Eight_LSBs,
  output [7:0] Eight_MSBs
);

  Register #(.width(16)) register_1 (.D(Data), .en(WE), .clk(clk), .Q(Result), .clr(reset));
  assign Dout = OE ? Result : 16'bz;  // Controlled_Buffer controlled_buffer_1
  BitSelector #(.group(8), .width(16)) bitselector_1 (.in(Dout), .out(Eight_LSBs), .sel(1'b0));
  BitSelector #(.group(8), .width(16)) bitselector_2 (.in(Dout), .out(Eight_MSBs), .sel(1'b1));
endmodule

module CPU (
  input  counter_OE,
  input  [7:0] RAM_test_data,
  input  counter_enable,
  input  RAM_test_OE,
  input  WE_MAR,
  input  Reset_MAR,
  input  RAM_WE,
  input  OE_MAR,
  input  [15:0] TestData,
  input  Test_OE,
  input  internal_OE_MBR,
  input  RAM_OE,
  input  WE_IR,
  input  clk,
  input  Reset_IR,
  input  WE_MBR,
  input  OE_IR,
  input  Reset_MBR,
  input  OE_MBR,
  input  WE_A,
  input  Reg_AB_Reset,
  input  Reg_AB_OE,
  input  WE_OR,
  input  Reset_OR,
  input  ALU_OE,
  input  [3:0] AUSel,
  input  OE_OR,
  input  [2:0] RUSel,
  input  WE_B,
  output [7:0] Result_MAR,
  output [3:0] counter_content,
  output [15:0] IR_Result,
  output [15:0] Result_MBR,
  output [15:0] Result_A,
  output [15:0] Result_OR,
  output [15:0] AUResult,
  output RUResult,
  output [15:0] Result_B
);

  wire [3:0] decimal_decoder_2_dout_2, decimal_decoder_2_dout_3;
  wire [7:0] controlled_buffer_1_out, decimal_decoder_2_dout, Instruction_Register_eight_lsbs, mar_1_dout;
  wire [15:0] ALU_audout, bit_extender_1_out, decimal_decoder_1_dout, decimal_decoder_3_dout,
       decimal_decoder_4_dout, ram_1_dout;

  Counter #(.max('hf), .width(4)) counter_1 (
    .count(counter_enable), .clk(clk), .D(controlled_buffer_1_out[3:0]), .Q(counter_content));  // open: clr, load, up, carry
  assign bit_extender_1_out = {{12{counter_content[3]}}, counter_content};  // Bit_Extender bit_extender_1
  assign controlled_buffer_1_out[3:0] = counter_OE ? counter_content : 4'bz;  // Controlled_Buffer controlled_buffer_1
  decimal_decoder decimal_decoder_1 (.Din(bit_extender_1_out), .Dout(decimal_decoder_1_dout));
  _7_Segment_Display u_7_segment_display_1 (
    .g(decimal_decoder_1_dout[7]), .f(decimal_decoder_1_dout[6]), .a(decimal_decoder_1_dout[5]),
    .b(decimal_decoder_1_dout[4]), .e(decimal_decoder_1_dout[15]), .d(decimal_decoder_1_dout[14]),
    .c(decimal_decoder_1_dout[13]), .dp(decimal_decoder_1_dout[12]));
  _7_Segment_Display u_7_segment_display_2 (
    .g(decimal_decoder_1_dout[3]), .f(decimal_decoder_1_dout[2]), .a(decimal_decoder_1_dout[1]),
    .b(decimal_decoder_1_dout[0]), .e(decimal_decoder_1_dout[11]), .d(decimal_decoder_1_dout[10]),
    .c(decimal_decoder_1_dout[9]), .dp(decimal_decoder_1_dout[8]));
  register_file Instruction_Register (
    .Data(ALU_audout), .WE(WE_IR), .clk(clk), .reset(Reset_IR), .OE(OE_IR), .Result(IR_Result),
    .Eight_LSBs(Instruction_Register_eight_lsbs));  // open: Dout, Eight_MSBs
  register_file A (
    .Data(ALU_audout), .WE(WE_A), .clk(clk), .reset(Reg_AB_Reset), .OE(Reg_AB_OE), .Result(Result_A));  // open: Dout, Eight_LSBs, Eight_MSBs
  project_alu ALU (
    .A(Result_A), .B(Result_B), .ALU_OE(ALU_OE), .AUSel(AUSel), .RUSel(RUSel), .AUResult(AUResult),
    .AUDout(ALU_audout), .RUResult(RUResult));
  register_file B (
    .Data(ALU_audout), .WE(WE_B), .clk(clk), .reset(Reg_AB_Reset), .OE(Reg_AB_OE), .Result(Result_B));  // open: Dout, Eight_LSBs, Eight_MSBs
  BitSelector #(.group(8)) bitselector_1 (
    .in(Instruction_Register_eight_lsbs), .out(controlled_buffer_1_out), .sel(1'b0));
  decimal_decoder decimal_decoder_2 (
    .Din(Result_A), .Dout({decimal_decoder_2_dout_3, decimal_decoder_2_dout_2, decimal_decoder_2_dout}));
  decimal_decoder decimal_decoder_3 (.Din(Result_B), .Dout(decimal_decoder_3_dout));
  _7_Segment_Display u_7_segment_display_3 (
    .g(decimal_decoder_2_dout[7]), .f(decimal_decoder_2_dout[6]), .a(decimal_decoder_2_dout[5]),
    .b(decimal_decoder_2_dout[4]), .e(decimal_decoder_2_dout_3[3]), .d(decimal_decoder_2_dout_3[2]),
    .c(decimal_decoder_2_dout_3[1]), .dp(decimal_decoder_2_dout_3[0]));
  _7_Segment_Display u_7_segment_display_4 (
    .g(decimal_decoder_2_dout[3]), .f(decimal_decoder_2_dout[2]), .a(decimal_decoder_2_dout[1]),
    .b(decimal_decoder_2_dout[0]), .e(decimal_decoder_2_dout_2[3]), .d(decimal_decoder_2_dout_2[2]),
    .c(decimal_decoder_2_dout_2[1]), .dp(decimal_decoder_2_dout_2[0]));
  _7_Segment_Display u_7_segment_display_5 (
    .g(decimal_decoder_3_dout[7]), .f(decimal_decoder_3_dout[6]), .a(decimal_decoder_3_dout[5]),
    .b(decimal_decoder_3_dout[4]), .e(decimal_decoder_3_dout[15]), .d(decimal_decoder_3_dout[14]),
    .c(decimal_decoder_3_dout[13]), .dp(decimal_decoder_3_dout[12]));
  _7_Segment_Display u_7_segment_display_6 (
    .g(decimal_decoder_3_dout[3]), .f(decimal_decoder_3_dout[2]), .a(decimal_decoder_3_dout[1]),
    .b(decimal_decoder_3_dout[0]), .e(decimal_decoder_3_dout[11]), .d(decimal_decoder_3_dout[10]),
    .c(decimal_decoder_3_dout[9]), .dp(decimal_decoder_3_dout[8]));
  LED led_1 (.in(ALU_audout[15]));
  LED led_2 (.in(ALU_audout[14]));
  assign ALU_audout = Test_OE ? TestData : 16'bz;  // Controlled_Buffer controlled_buffer_2
  LED led_3 (.in(ALU_audout[13]));
  LED led_4 (.in(ALU_audout[12]));
  LED led_5 (.in(ALU_audout[11]));
  LED led_6 (.in(ALU_audout[10]));
  LED led_7 (.in(ALU_audout[9]));
  LED led_8 (.in(ALU_audout[8]));
  LED led_9 (.in(ALU_audout[7]));
  LED led_10 (.in(ALU_audout[6]));
  LED led_11 (.in(ALU_audout[5]));
  LED led_12 (.in(ALU_audout[4]));
  LED led_13 (.in(ALU_audout[3]));
  LED led_14 (.in(ALU_audout[2]));
  LED led_15 (.in(ALU_audout[1]));
  LED led_16 (.in(ALU_audout[0]));
  assign ALU_audout = internal_OE_MBR ? Result_MBR : 16'bz;  // Controlled_Buffer controlled_buffer_3
  MAR mar_1 (
    .Data(controlled_buffer_1_out), .WE(WE_MAR), .clk(clk), .reset(Reset_MAR), .OE(OE_MAR),
    .Result(Result_MAR), .Dout(mar_1_dout));
  register_file MBR (
    .Data(ALU_audout), .WE(WE_MBR), .clk(clk), .reset(Reset_MBR), .OE(OE_MBR), .Result(Result_MBR),
    .Dout(ALU_audout));  // open: Eight_LSBs, Eight_MSBs
  register_file Output_Register (
    .Data(ALU_audout), .WE(WE_OR), .clk(clk), .reset(Reset_OR), .OE(OE_OR), .Result(Result_OR),
    .Dout(ALU_audout));  // open: Eight_LSBs, Eight_MSBs
  decimal_decoder decimal_decoder_4 (.Din(Result_OR), .Dout(decimal_decoder_4_dout));
  LED led_17 (.in(ALU_audout[15]));
  LED led_18 (.in(ALU_audout[14]));
  assign mar_1_dout = RAM_test_OE ? RAM_test_data : 8'bz;  // Controlled_Buffer controlled_buffer_4
  LED led_19 (.in(ALU_audout[13]));
  _7_Segment_Display u_7_segment_display_7 (
    .g(decimal_decoder_4_dout[7]), .f(decimal_decoder_4_dout[6]), .a(decimal_decoder_4_dout[5]),
    .b(decimal_decoder_4_dout[4]), .e(decimal_decoder_4_dout[15]), .d(decimal_decoder_4_dout[14]),
    .c(decimal_decoder_4_dout[13]), .dp(decimal_decoder_4_dout[12]));
  LED led_20 (.in(ALU_audout[12]));
  LED led_21 (.in(ALU_audout[11]));
  _7_Segment_Display u_7_segment_display_8 (
    .g(decimal_decoder_4_dout[3]), .f(decimal_decoder_4_dout[2]), .a(decimal_decoder_4_dout[1]),
    .b(decimal_decoder_4_dout[0]), .e(decimal_decoder_4_dout[11]), .d(decimal_decoder_4_dout[10]),
    .c(decimal_decoder_4_dout[9]), .dp(decimal_decoder_4_dout[8]));
  LED led_22 (.in(ALU_audout[10]));
  LED led_23 (.in(ALU_audout[9]));
  LED led_24 (.in(ALU_audout[8]));
  LED led_25 (.in(ALU_audout[7]));
  LED led_26 (.in(ALU_audout[6]));
  LED led_27 (.in(ALU_audout[5]));
  LED led_28 (.in(ALU_audout[4]));
  LED led_29 (.in(ALU_audout[3]));
  LED led_30 (.in(ALU_audout[2]));
  LED led_31 (.in(ALU_audout[1]));
  LED led_32 (.in(ALU_audout[0]));
  RAM #(.asyncread("true"), .dataWidth(16), .\type ("nonvolatile")) ram_1 (
    .addr(mar_1_dout), .we(RAM_WE), .clk(clk), .din(ALU_audout), .dout(ram_1_dout));  // open: oe
  assign ALU_audout = RAM_OE ? ram_1_dout : 16'bz;  // Controlled_Buffer controlled_buffer_5

  // Notes on the sheet:
  //   D14
  //   D15
  //   D13
  //   D12
  //   D11
  //   D10
  //   D9
  //   Internal Data Bus
  //   D8
  //   D7
  //   D6
  //   D5
  //   D4
  //   D3
  //   D2
  //   D1
  //   D0
  //   External Data Bus
  //   D14
  //   D15
  //   D13
  //   D12
  //   D11
  //   D10
  //   D9
  //   D8
  //   D7
  //   D6
  //   D5
  //   D4
  //   D3
  //   D2
  //   D1
  //   D0
endmodule

module MAR (
  input  [7:0] Data,
  input  WE,
  input  clk,
  input  reset,
  input  OE,
  output [7:0] Result,
  output [7:0] Dout
);

  Register register_1 (.D(Data), .en(WE), .clk(clk), .Q(Result), .clr(reset));
  assign Dout = OE ? Result : 8'bz;  // Controlled_Buffer controlled_buffer_1
endmodule

module decimal_decoder (
  input  [15:0] Din,
  output [15:0] Dout
);

  ROM #(.addrWidth(16), .dataWidth(16)) rom_1 (.addr(Din), .data({Dout[15:12], Dout[7:4], Dout[11:8], Dout[3:0]}));

  // Notes on the sheet:
  //   contents of rom_1 (hex, n*v repeats v):
  //   e7 21 cb 6b 2d 6e ee 23 ef 2f 21e7 2121 21cb 216b 212d 216e 21ee 2123 21ef 212f cbe7 cb21 cbcb cb6b
  //   cb2d cb6e cbee cb23 cbef cb2f 6be7 6b21 6bcb 6b6b 6b2d 6b6e 6bee 6b23 6bef 6b2f 2de7 2d21 2dcb 2d6b
  //   2d2d 2d6e 2dee 2d23 2def 2d2f 6ee7 6e21 6ecb 6e6b 6e2d 6e6e 6eee 6e23 6eef 6e2f eee7 ee21 eecb ee6b
  //   ee2d ee6e eeee ee23 eeef ee2f 23e7 2321 23cb 236b 232d 236e 23ee 2323 23ef 232f efe7 ef21 efcb ef6b
  //   ef2d ef6e efee ef23 efef ef2f 2fe7 2f21 2fcb 2f6b 2f2d 2f6e 2fee 2f23 2fef 2f2f e7e7 e721 e7cb e76b
  //   e72d e76e e7ee e723 e7ef e72f 21e7 2121 21cb 216b 212d 216e 21ee 2123 21ef 212f cbe7 cb21 cbcb cb6b
  //   cb2d cb6e cbee cb23 cbef cb2f 6be7 6b21 6bcb 6b6b 6b2d 6b6e 6bee 6b23 6bef 6b2f 2de7 2d21 2dcb 2d6b
  //   2d2d 2d6e 2dee 2d23 2def 2d2f 6ee7 6e21 6ecb 6e6b 6e2d 6e6e 6eee 6e23 6eef 6e2f eee7 ee21 eecb ee6b
  //   ee2d ee6e eeee ee23 eeef ee2f 23e7 2321 23cb 236b 232d 236e 23ee 2323 23ef 232f efe7 ef21 efcb ef6b
  //   ef2d ef6e efee ef23 efef ef2f 2fe7 2f21 2fcb 2f6b 2f2d 2f6e 2fee 2f23 2fef 2f2f e7e7 e721 e7cb e76b
  //   e72d e76e e7ee e723 e7ef e72f 21e7 2121 21cb 216b 212d 216e 21ee 2123 21ef 212f cbe7 cb21 cbcb cb6b
  //   cb2d cb6e cbee cb23 cbef cb2f 6be7 6b21 6bcb 6b6b 6b2d 6b6e 6bee 6b23 6bef 6b2f 2de7 2d21 2dcb 2d6b
  //   2d2d 2d6e 2dee 2d23 2def 2d2f 6ee7 6e21 6ecb 6e6b 6e2d 6e6e
endmodule
